// Logisim project cpu1.circ as structural Verilog: 1 circuit, main circuit main
module main (
);

  wire add_out, controlled_buffer_1_out, cpy_out, div_out, from_alu0_out, from_alu1_out, from_alu2_out,
       from_out0_out, from_reg1_out, from_reg2_out, from_reg3_out, from_reg4_out, from_reg5_out,
       from_reg6_out, gto_out, hlt_out, imm_out, main_sys_clock_out, mlt_out, multiplexer_1_out, not_1_out,
       not_2_out, not_3_out, not_4_out, not_5_out, not_6_out, not_7_out, not_8_out, not_9_out, not_10_out,
       not_11_out, not_12_out, not_13_out, not_14_out, not_15_out, not_16_out, not_17_out, not_18_out,
       not_19_out, not_20_out, not_21_out, not_22_out, not_23_out, not_24_out, not_25_out, not_26_out,
       not_27_out, not_28_out, not_29_out, not_30_out, not_31_out, not_32_out, not_33_out, not_34_out,
       not_35_out, not_36_out, not_37_out, not_38_out, not_39_out, not_40_out, not_41_out, not_42_out,
       not_43_out, not_44_out, not_45_out, not_46_out, not_47_out, not_48_out, not_49_out, not_50_out,
       not_51_out, not_52_out, not_53_out, not_54_out, not_55_out, not_56_out, not_57_out, not_58_out,
       not_59_out, not_60_out, not_61_out, not_62_out, not_63_out, not_64_out, not_65_out, not_66_out,
       not_67_out, not_68_out, not_69_out, not_70_out, not_71_out, not_72_out, not_73_out, not_74_out,
       not_75_out, not_76_out, not_77_out, not_78_out, not_79_out, not_80_out, not_81_out, not_82_out,
       not_83_out, not_84_out, not_85_out, not_86_out, not_87_out, not_88_out, not_89_out, not_90_out,
       not_91_out, not_92_out, not_93_out, not_94_out, not_95_out, not_96_out, not_97_out, not_98_out,
       not_99_out, not_100_out, not_101_out, not_102_out, not_103_out, not_104_out, not_105_out, not_106_out,
       not_107_out, not_108_out, not_109_out, not_110_out, not_111_out, not_112_out, not_113_out,
       not_114_out, not_115_out, not_116_out, not_117_out, or_1_out, or_4_out, rst_out, sub_out, to_alu0_out,
       to_alu1_out, to_alu2_out, to_out0_out, to_reg0_out, to_reg1_out, to_reg2_out, to_reg3_out,
       to_reg4_out, to_reg5_out, to_reg6_out;
  wire [1:0] or_3_out;
  wire [3:0] or_5_out;
  wire [11:0] counter_1_q;
  wire [15:0] adder_1_out, alu0_q, alu1_q, alu2_q, divider_1_out, multiplexer_2_out, multiplexer_3_out,
       multiplexer_4_out, multiplexer_5_out, multiplier_1_out, out0_q, reg0_q, reg1_q, reg2_q, reg3_q,
       reg4_q, reg5_q, reg6_q, rom_1_data, subtractor_1_out;

  Clock main_sys_clock (.out(main_sys_clock_out));
  assign controlled_buffer_1_out = not_1_out ? main_sys_clock_out : 1'bz;  // Controlled_Buffer controlled_buffer_1
  not not_1 (not_1_out, hlt_out);
  Counter #(.max('hfff), .width(12)) counter_1 (
    .clr(rst_out), .load(gto_out), .clk(controlled_buffer_1_out), .D(rom_1_data[11:0]), .Q(counter_1_q));  // open: up, count, carry
  ROM #(.addrWidth(12), .dataWidth(16)) rom_1 (.addr(counter_1_q), .data(rom_1_data));
  not not_2 (not_2_out, rom_1_data[12]);
  not not_3 (not_3_out, rom_1_data[13]);
  not not_4 (not_4_out, rom_1_data[14]);
  not not_5 (not_5_out, rom_1_data[15]);
  not not_6 (not_6_out, rom_1_data[13]);
  and imm (imm_out, not_2_out, not_3_out, not_4_out, not_5_out);
  and cpy (cpy_out, rom_1_data[12], not_6_out, not_7_out, not_8_out);
  Multiplexer #(.enable("true")) multiplexer_1 (
    .in0(imm_out), .in1(to_reg0_out), .out(multiplexer_1_out), .sel(cpy_out));  // open: en
  not not_7 (not_7_out, rom_1_data[14]);
  not not_8 (not_8_out, rom_1_data[15]);
  not not_9 (not_9_out, rom_1_data[12]);
  not not_10 (not_10_out, rom_1_data[14]);
  not not_11 (not_11_out, rom_1_data[15]);
  not not_12 (not_12_out, rom_1_data[12]);
  and add (add_out, not_9_out, rom_1_data[13], not_10_out, not_11_out);
  not not_13 (not_13_out, rom_1_data[5]);
  not not_14 (not_14_out, rom_1_data[4]);
  not not_15 (not_15_out, rom_1_data[3]);
  not not_16 (not_16_out, rom_1_data[2]);
  not not_17 (not_17_out, rom_1_data[1]);
  and to_reg0 (to_reg0_out, not_13_out, not_14_out, not_15_out, not_16_out, not_17_out, rom_1_data[0]);
  not not_18 (not_18_out, rom_1_data[13]);
  not not_19 (not_19_out, rom_1_data[15]);
  not not_20 (not_20_out, rom_1_data[12]);
  not not_21 (not_21_out, rom_1_data[13]);
  not not_22 (not_22_out, rom_1_data[14]);
  and sub (sub_out, not_12_out, not_18_out, rom_1_data[14], not_19_out);
  and mlt (mlt_out, not_20_out, not_21_out, not_22_out, rom_1_data[15]);
  not not_23 (not_23_out, rom_1_data[5]);
  not not_24 (not_24_out, rom_1_data[4]);
  not not_25 (not_25_out, rom_1_data[3]);
  not not_26 (not_26_out, rom_1_data[2]);
  and to_reg1 (to_reg1_out, not_23_out, not_24_out, not_25_out, not_26_out, rom_1_data[1], not_30_out);
  not not_27 (not_27_out, rom_1_data[13]);
  not not_28 (not_28_out, rom_1_data[14]);
  not not_29 (not_29_out, rom_1_data[12]);
  and div (div_out, rom_1_data[12], not_27_out, not_28_out, rom_1_data[15]);
  not not_30 (not_30_out, rom_1_data[0]);
  not not_31 (not_31_out, rom_1_data[5]);
  not not_32 (not_32_out, rom_1_data[4]);
  not not_33 (not_33_out, rom_1_data[3]);
  not not_34 (not_34_out, rom_1_data[1]);
  and to_reg2 (to_reg2_out, not_31_out, not_32_out, not_33_out, rom_1_data[2], not_34_out, not_39_out);
  not not_35 (not_35_out, or_4_out);
  or or_1 (or_1_out, or_4_out, to_alu2_out);
  not not_36 (not_36_out, rom_1_data[14]);
  not not_37 (not_37_out, rom_1_data[12]);
  not not_38 (not_38_out, rom_1_data[13]);
  and gto (gto_out, not_29_out, rom_1_data[13], not_36_out, rom_1_data[15]);
  and rst (rst_out, not_37_out, not_38_out, rom_1_data[14], rom_1_data[15]);
  not not_39 (not_39_out, rom_1_data[0]);
  not not_40 (not_40_out, rom_1_data[5]);
  not not_41 (not_41_out, rom_1_data[4]);
  not not_42 (not_42_out, rom_1_data[2]);
  not not_43 (not_43_out, rom_1_data[1]);
  and to_reg3 (to_reg3_out, not_40_out, not_41_out, rom_1_data[3], not_42_out, not_43_out, not_45_out);
  Adder #(.width(16)) adder_1 (.a(alu0_q), .b(alu1_q), .out(adder_1_out));  // open: cin, cout
  Subtractor #(.width(16)) subtractor_1 (.a(alu0_q), .b(alu1_q), .out(subtractor_1_out));  // open: bin, bout
  Multiplier #(.width(16)) multiplier_1 (.a(alu0_q), .b(alu1_q), .out(multiplier_1_out));  // open: cin, cout
  Divider #(.width(16)) divider_1 (.a(alu0_q), .b(alu1_q), .out(divider_1_out));  // open: upper, rem
  not not_44 (not_44_out, imm_out);
  Register #(.width(16)) reg0 (
    .D(multiplexer_3_out), .en(multiplexer_1_out), .clk(controlled_buffer_1_out), .Q(reg0_q));  // open: clr
  Register #(.width(16)) reg1 (
    .D(multiplexer_3_out), .en(to_reg1_out), .clk(controlled_buffer_1_out), .Q(reg1_q));  // open: clr
  Register #(.width(16)) reg2 (
    .D(multiplexer_3_out), .en(to_reg2_out), .clk(controlled_buffer_1_out), .Q(reg2_q));  // open: clr
  Register #(.width(16)) reg3 (
    .D(multiplexer_3_out), .en(to_reg3_out), .clk(controlled_buffer_1_out), .Q(reg3_q));  // open: clr
  Register #(.width(16)) reg4 (
    .D(multiplexer_3_out), .en(to_reg4_out), .clk(controlled_buffer_1_out), .Q(reg4_q));  // open: clr
  Register #(.width(16)) reg5 (
    .D(multiplexer_3_out), .en(to_reg5_out), .clk(controlled_buffer_1_out), .Q(reg5_q));  // open: clr
  Register #(.width(16)) reg6 (
    .D(multiplexer_3_out), .en(to_reg6_out), .clk(controlled_buffer_1_out), .Q(reg6_q));  // open: clr
  Register #(.width(16)) alu0 (
    .D(multiplexer_3_out), .en(to_alu0_out), .clk(controlled_buffer_1_out), .Q(alu0_q));  // open: clr
  Register #(.width(16)) alu1 (
    .D(multiplexer_3_out), .en(to_alu1_out), .clk(controlled_buffer_1_out), .Q(alu1_q));  // open: clr
  Register #(.width(16)) alu2 (
    .D(multiplexer_2_out), .en(or_1_out), .clk(controlled_buffer_1_out), .Q(alu2_q));  // open: clr
  Multiplexer #(.width(16)) multiplexer_2 (
    .in0(multiplexer_4_out), .in1(multiplexer_3_out), .out(multiplexer_2_out), .sel(not_35_out));
  Register #(.width(16)) out0 (
    .D(multiplexer_3_out), .en(to_out0_out), .clk(controlled_buffer_1_out), .Q(out0_q));  // open: clr
  and hlt (hlt_out, rom_1_data[12], rom_1_data[13], rom_1_data[14], rom_1_data[15]);
  not not_45 (not_45_out, rom_1_data[0]);
  not not_46 (not_46_out, rom_1_data[5]);
  not not_47 (not_47_out, rom_1_data[3]);
  not not_48 (not_48_out, rom_1_data[2]);
  not not_49 (not_49_out, rom_1_data[1]);
  and to_reg4 (to_reg4_out, not_46_out, rom_1_data[4], not_47_out, not_48_out, not_49_out, not_50_out);
  Multiplexer #(.width(16)) multiplexer_3 (
    .in0(rom_1_data), .in1(multiplexer_5_out), .out(multiplexer_3_out), .sel(not_44_out));
  not not_50 (not_50_out, rom_1_data[0]);
  not not_51 (not_51_out, rom_1_data[4]);
  not not_52 (not_52_out, rom_1_data[3]);
  not not_53 (not_53_out, rom_1_data[2]);
  not not_54 (not_54_out, rom_1_data[1]);
  and to_reg5 (to_reg5_out, rom_1_data[5], not_51_out, not_52_out, not_53_out, not_54_out, not_55_out);
  Multiplexer #(.select(2), .width(16)) multiplexer_4 (
    .in0(adder_1_out), .in1(subtractor_1_out), .in2(multiplier_1_out), .out(multiplexer_4_out), .sel(or_3_out));  // open: in3
  not not_55 (not_55_out, rom_1_data[0]);
  not not_56 (not_56_out, rom_1_data[5]);
  not not_57 (not_57_out, rom_1_data[4]);
  not not_58 (not_58_out, rom_1_data[3]);
  not not_59 (not_59_out, rom_1_data[2]);
  and to_reg6 (to_reg6_out, not_56_out, not_57_out, not_58_out, not_59_out, rom_1_data[1], rom_1_data[0]);
  Multiplexer #(.select(4), .width(16)) multiplexer_5 (
    .in0(reg0_q), .in1(reg1_q), .in2(reg2_q), .in3(reg3_q), .in4(reg4_q), .in5(reg5_q), .in6(reg6_q),
    .in7(alu0_q), .in8(alu1_q), .in9(alu2_q), .in10(out0_q), .out(multiplexer_5_out), .sel(or_5_out));  // open: in11, in12, in13, in14, in15
  not not_60 (not_60_out, rom_1_data[5]);
  not not_61 (not_61_out, rom_1_data[4]);
  not not_62 (not_62_out, rom_1_data[3]);
  and to_alu0 (to_alu0_out, not_60_out, not_61_out, not_62_out, rom_1_data[2], rom_1_data[1], not_63_out);
  or or_2 (or_3_out[1], sub_out, div_out);
  or or_3 (or_3_out[0], mlt_out, div_out);
  not not_63 (not_63_out, rom_1_data[0]);
  not not_64 (not_64_out, rom_1_data[5]);
  not not_65 (not_65_out, rom_1_data[4]);
  not not_66 (not_66_out, rom_1_data[1]);
  and to_alu1 (to_alu1_out, not_64_out, not_65_out, rom_1_data[3], rom_1_data[2], not_66_out, not_67_out);
  not not_67 (not_67_out, rom_1_data[0]);
  not not_68 (not_68_out, rom_1_data[5]);
  not not_69 (not_69_out, rom_1_data[2]);
  not not_70 (not_70_out, rom_1_data[1]);
  and to_alu2 (to_alu2_out, not_68_out, rom_1_data[4], rom_1_data[3], not_69_out, not_70_out, not_71_out);
  or or_4 (or_4_out, mlt_out, div_out, sub_out, add_out);
  not not_71 (not_71_out, rom_1_data[0]);
  and to_out0 (to_out0_out, rom_1_data[5], rom_1_data[4], rom_1_data[3], rom_1_data[2], rom_1_data[1], rom_1_data[0]);
  not not_72 (not_72_out, rom_1_data[11]);
  not not_73 (not_73_out, rom_1_data[10]);
  not not_74 (not_74_out, rom_1_data[9]);
  not not_75 (not_75_out, rom_1_data[8]);
  not not_76 (not_76_out, rom_1_data[7]);
  // AND_Gate from_reg0 has open pins: in0=not_72_out, in1=not_73_out, in2=not_74_out, in3=not_75_out, in4=not_76_out, in5=rom_1_data[6], out=open
  or or_5 (or_5_out[0], from_reg1_out, from_reg3_out, from_alu2_out, from_reg5_out, from_alu0_out);
  not not_77 (not_77_out, rom_1_data[11]);
  not not_78 (not_78_out, rom_1_data[10]);
  not not_79 (not_79_out, rom_1_data[9]);
  not not_80 (not_80_out, rom_1_data[8]);
  and from_reg1 (from_reg1_out, not_77_out, not_78_out, not_79_out, not_80_out, rom_1_data[7], not_81_out);
  or or_6 (or_5_out[1], from_reg2_out, from_reg3_out, from_out0_out, from_reg6_out, from_alu0_out);
  not not_81 (not_81_out, rom_1_data[6]);
  not not_82 (not_82_out, rom_1_data[11]);
  or or_7 (or_5_out[2], from_reg4_out, from_reg5_out, from_reg6_out, from_alu0_out);
  not not_83 (not_83_out, rom_1_data[10]);
  not not_84 (not_84_out, rom_1_data[9]);
  not not_85 (not_85_out, rom_1_data[7]);
  not not_86 (not_86_out, rom_1_data[6]);
  and from_reg2 (from_reg2_out, not_82_out, not_83_out, not_84_out, rom_1_data[8], not_85_out, not_86_out);
  or or_8 (or_5_out[3], from_alu2_out, from_alu1_out, from_out0_out);
  not not_87 (not_87_out, rom_1_data[11]);
  not not_88 (not_88_out, rom_1_data[10]);
  not not_89 (not_89_out, rom_1_data[8]);
  and from_reg3 (from_reg3_out, not_87_out, not_88_out, rom_1_data[9], not_89_out, not_90_out, not_91_out);
  not not_90 (not_90_out, rom_1_data[7]);
  not not_91 (not_91_out, rom_1_data[6]);
  not not_92 (not_92_out, rom_1_data[11]);
  not not_93 (not_93_out, rom_1_data[9]);
  not not_94 (not_94_out, rom_1_data[8]);
  not not_95 (not_95_out, rom_1_data[7]);
  not not_96 (not_96_out, rom_1_data[6]);
  and from_reg4 (from_reg4_out, not_92_out, rom_1_data[10], not_93_out, not_94_out, not_95_out, not_96_out);
  not not_97 (not_97_out, rom_1_data[10]);
  not not_98 (not_98_out, rom_1_data[9]);
  not not_99 (not_99_out, rom_1_data[8]);
  and from_reg5 (from_reg5_out, rom_1_data[11], not_97_out, not_98_out, not_99_out, not_100_out, not_101_out);
  not not_100 (not_100_out, rom_1_data[7]);
  not not_101 (not_101_out, rom_1_data[6]);
  not not_102 (not_102_out, rom_1_data[11]);
  not not_103 (not_103_out, rom_1_data[10]);
  not not_104 (not_104_out, rom_1_data[9]);
  not not_105 (not_105_out, rom_1_data[8]);
  and from_reg6 (from_reg6_out, not_102_out, not_103_out, not_104_out, not_105_out, rom_1_data[7], rom_1_data[6]);
  not not_106 (not_106_out, rom_1_data[11]);
  not not_107 (not_107_out, rom_1_data[10]);
  not not_108 (not_108_out, rom_1_data[9]);
  and from_alu0 (from_alu0_out, not_106_out, not_107_out, not_108_out, rom_1_data[8], rom_1_data[7], not_109_out);
  not not_109 (not_109_out, rom_1_data[6]);
  not not_110 (not_110_out, rom_1_data[11]);
  not not_111 (not_111_out, rom_1_data[10]);
  not not_112 (not_112_out, rom_1_data[7]);
  not not_113 (not_113_out, rom_1_data[6]);
  and from_alu1 (from_alu1_out, not_110_out, not_111_out, rom_1_data[9], rom_1_data[8], not_112_out, not_113_out);
  not not_114 (not_114_out, rom_1_data[11]);
  not not_115 (not_115_out, rom_1_data[8]);
  and from_alu2 (from_alu2_out, not_114_out, rom_1_data[10], rom_1_data[9], not_115_out, not_116_out, not_117_out);
  not not_116 (not_116_out, rom_1_data[7]);
  not not_117 (not_117_out, rom_1_data[6]);
  and from_out0 (from_out0_out, rom_1_data[11], rom_1_data[10], rom_1_data[9], rom_1_data[8], rom_1_data[7], rom_1_data[6]);
endmodule
