// Digital circuit pcv1.dig as structural Verilog
module pcv1 (
  input  in_1,
  input  in_2,
  input  in_3,
  input  in_4,
  input  in_5,
  input  in_6,
  input  in_7,
  input  in_8,
  input  in_9,
  input  in_10,
  input  in_11,
  input  in_12,
  input  in_13,
  input  in_14,
  input  in_15,
  input  in_16
);

  wire and_1_out, and_2_out, and_3_out, and_4_out, and_5_out, and_6_out, and_7_out, and_8_out, and_9_out,
       and_10_out, and_11_out, and_12_out, and_13_out, and_14_out, and_15_out, and_16_out, and_17_out,
       and_18_out, and_19_out, and_20_out, and_21_out, and_22_out, and_23_out, and_24_out, and_25_out,
       and_26_out, and_27_out, and_28_out, and_29_out, and_30_out, and_31_out, and_32_out, and_33_out,
       and_34_out, and_35_out, and_36_out, and_37_out, and_38_out, and_39_out, and_40_out, and_41_out,
       and_42_out, and_43_out, and_44_out, and_45_out, and_46_out, and_47_out, and_60_out, and_61_out,
       and_62_out, and_63_out, and_64_out, and_65_out, and_66_out, and_67_out, and_68_out, and_69_out,
       and_70_out, and_71_out, and_72_out, and_73_out, and_74_out, and_75_out, and_76_out, and_77_out,
       and_78_out, and_79_out, and_80_out, and_81_out, and_82_out, and_83_out, and_84_out, and_85_out,
       and_86_out, and_87_out, and_88_out, and_89_out, and_90_out, and_91_out, and_92_out, and_93_out,
       and_94_out, and_95_out, and_96_out, and_97_out, and_98_out, and_99_out, and_100_out, and_101_out,
       and_102_out, and_103_out, and_104_out, and_105_out, and_106_out, and_107_out, and_108_out,
       and_109_out, and_110_out, and_111_out, and_112_out, and_113_out, and_114_out, and_115_out,
       and_116_out, and_117_out, and_118_out, and_119_out, and_120_out, and_121_out, and_122_out,
       and_123_out, and_124_out, and_125_out, and_126_out, and_127_out, nor_1_out, nor_2_out, nor_3_out,
       nor_5_out, nor_7_out, nor_9_out, nor_11_out, nor_13_out, nor_15_out, nor_17_out, nor_19_out,
       nor_21_out, nor_23_out, nor_25_out, nor_27_out, nor_29_out, nor_31_out, nor_33_out, nor_35_out,
       nor_37_out, nor_39_out, nor_41_out, nor_43_out, nor_45_out, nor_47_out, nor_49_out, nor_51_out,
       nor_53_out, nor_55_out, nor_57_out, nor_59_out, nor_61_out, not_1_out, not_2_out, not_3_out,
       not_4_out, not_5_out, not_6_out, not_7_out, not_8_out, not_9_out, not_10_out, not_11_out, not_12_out,
       not_13_out, not_14_out, not_15_out, not_16_out, not_17_out, not_18_out, not_19_out, not_20_out,
       not_21_out, not_22_out, not_23_out, not_24_out, not_25_out, not_26_out, or_1_out, or_2_out, or_3_out,
       or_4_out, or_5_out, or_6_out, or_7_out, or_8_out, or_9_out, or_10_out, or_11_out, or_12_out,
       or_13_out, or_14_out, or_15_out, or_16_out, undriven, undriven_2, undriven_3, undriven_4, undriven_5,
       undriven_6, undriven_7, undriven_8, undriven_9, undriven_10, undriven_11, undriven_12, undriven_13,
       undriven_14, undriven_15, undriven_16, undriven_17, undriven_18, undriven_19, undriven_20,
       undriven_21, undriven_22, undriven_23, undriven_24, undriven_25, undriven_26, undriven_27,
       undriven_28, undriven_29, undriven_30, undriven_31, undriven_32, undriven_33, undriven_34,
       undriven_35, xor_1_out, xor_2_out, xor_3_out, xor_4_out, xor_5_out, xor_6_out, xor_7_out, xor_8_out,
       xor_9_out, xor_10_out, xor_11_out, xor_12_out, xor_13_out, xor_14_out, xor_15_out, xor_16_out,
       xor_17_out, xor_18_out, xor_19_out, xor_20_out, xor_21_out, xor_22_out, xor_23_out, xor_24_out,
       xor_25_out, xor_26_out, xor_27_out, xor_28_out, xor_29_out, xor_30_out, xor_31_out, xor_32_out;

  not not_1 (not_1_out, in_1);
  not not_2 (not_2_out, in_2);
  not not_3 (not_3_out, in_4);
  not not_4 (not_4_out, in_3);
  and and_1 (and_1_out, not_3_out, not_4_out, not_2_out, not_1_out);
  not not_5 (not_5_out, in_3);
  not not_6 (not_6_out, in_2);
  not not_7 (not_7_out, in_4);
  not not_8 (not_8_out, in_1);
  not not_9 (not_9_out, in_2);
  and and_2 (and_2_out, not_7_out, not_5_out, not_6_out, in_1);
  not not_10 (not_10_out, in_4);
  and and_3 (and_3_out, not_10_out, in_3, not_9_out, not_8_out);
  and and_4 (and_4_out, in_5, and_1_out);
  and and_5 (and_5_out, in_6, and_1_out);
  and and_6 (and_6_out, in_7, and_1_out);
  and and_7 (and_7_out, in_8, and_1_out);
  and and_8 (and_8_out, in_9, and_1_out);
  and and_9 (and_9_out, in_10, and_1_out);
  and and_10 (and_10_out, in_11, and_1_out);
  and and_11 (and_11_out, in_12, and_1_out);
  and and_12 (and_12_out, in_13, and_1_out);
  and and_13 (and_13_out, in_14, and_1_out);
  and and_14 (and_14_out, in_15, and_1_out);
  and and_15 (and_15_out, in_16, and_1_out);
  not not_11 (not_11_out, and_63_out);
  and and_16 (and_16_out, and_1_out, and_63_out);
  nor nor_1 (nor_1_out, nor_2_out, and_16_out);
  and and_17 (and_17_out, not_11_out, and_1_out);
  nor nor_2 (nor_2_out, and_17_out, nor_1_out);
  not not_12 (not_12_out, and_62_out);
  and and_18 (and_18_out, and_1_out, and_62_out);
  nor nor_3 (nor_3_out, nor_5_out, and_18_out);
  nor nor_4 (nor_3_out, nor_5_out, and_18_out);
  and and_19 (and_19_out, not_12_out, and_1_out);
  nor nor_5 (nor_5_out, and_19_out, nor_3_out);
  nor nor_6 (nor_5_out, and_19_out, nor_3_out);
  and and_20 (and_20_out, and_1_out, and_61_out);
  nor nor_7 (nor_7_out, nor_11_out, and_20_out);
  nor nor_8 (nor_7_out, nor_11_out, and_20_out);
  not not_13 (not_13_out, and_61_out);
  and and_21 (and_21_out, and_1_out, and_60_out);
  and and_22 (and_22_out, not_13_out, and_1_out);
  nor nor_9 (nor_9_out, nor_13_out, and_21_out);
  nor nor_10 (nor_9_out, nor_13_out, and_21_out);
  nor nor_11 (nor_11_out, and_22_out, nor_7_out);
  nor nor_12 (nor_11_out, and_22_out, nor_7_out);
  not not_14 (not_14_out, and_60_out);
  and and_23 (and_23_out, not_14_out, and_1_out);
  nor nor_13 (nor_13_out, and_23_out, nor_9_out);
  nor nor_14 (nor_13_out, and_23_out, nor_9_out);
  not not_15 (not_15_out, and_4_out);
  and and_24 (and_24_out, and_1_out, and_4_out);
  nor nor_15 (nor_15_out, nor_17_out, and_24_out);
  nor nor_16 (nor_15_out, nor_17_out, and_24_out);
  and and_25 (and_25_out, not_15_out, and_1_out);
  nor nor_17 (nor_17_out, and_25_out, nor_15_out);
  nor nor_18 (nor_17_out, and_25_out, nor_15_out);
  not not_16 (not_16_out, and_5_out);
  and and_26 (and_26_out, and_1_out, and_5_out);
  nor nor_19 (nor_19_out, nor_21_out, and_26_out);
  nor nor_20 (nor_19_out, nor_21_out, and_26_out);
  and and_27 (and_27_out, not_16_out, and_1_out);
  nor nor_21 (nor_21_out, and_27_out, nor_19_out);
  nor nor_22 (nor_21_out, and_27_out, nor_19_out);
  and and_28 (and_28_out, and_1_out, and_6_out);
  nor nor_23 (nor_23_out, nor_27_out, and_28_out);
  nor nor_24 (nor_23_out, nor_27_out, and_28_out);
  not not_17 (not_17_out, and_6_out);
  and and_29 (and_29_out, not_17_out, and_1_out);
  and and_30 (and_30_out, and_1_out, and_7_out);
  nor nor_25 (nor_25_out, nor_29_out, and_30_out);
  nor nor_26 (nor_25_out, nor_29_out, and_30_out);
  nor nor_27 (nor_27_out, and_29_out, nor_23_out);
  nor nor_28 (nor_27_out, and_29_out, nor_23_out);
  not not_18 (not_18_out, and_7_out);
  and and_31 (and_31_out, not_18_out, and_1_out);
  nor nor_29 (nor_29_out, and_31_out, nor_25_out);
  nor nor_30 (nor_29_out, and_31_out, nor_25_out);
  not not_19 (not_19_out, and_8_out);
  and and_32 (and_32_out, and_1_out, and_8_out);
  nor nor_31 (nor_31_out, nor_33_out, and_32_out);
  nor nor_32 (nor_31_out, nor_33_out, and_32_out);
  and and_33 (and_33_out, not_19_out, and_1_out);
  nor nor_33 (nor_33_out, and_33_out, nor_31_out);
  nor nor_34 (nor_33_out, and_33_out, nor_31_out);
  and and_34 (and_34_out, and_1_out, and_9_out);
  nor nor_35 (nor_35_out, nor_39_out, and_34_out);
  nor nor_36 (nor_35_out, nor_39_out, and_34_out);
  not not_20 (not_20_out, and_9_out);
  and and_35 (and_35_out, not_20_out, and_1_out);
  and and_36 (and_36_out, and_1_out, and_10_out);
  nor nor_37 (nor_37_out, nor_41_out, and_36_out);
  nor nor_38 (nor_37_out, nor_41_out, and_36_out);
  nor nor_39 (nor_39_out, and_35_out, nor_35_out);
  nor nor_40 (nor_39_out, and_35_out, nor_35_out);
  not not_21 (not_21_out, and_10_out);
  and and_37 (and_37_out, not_21_out, and_1_out);
  nor nor_41 (nor_41_out, and_37_out, nor_37_out);
  nor nor_42 (nor_41_out, and_37_out, nor_37_out);
  not not_22 (not_22_out, and_11_out);
  and and_38 (and_38_out, and_1_out, and_11_out);
  nor nor_43 (nor_43_out, nor_45_out, and_38_out);
  nor nor_44 (nor_43_out, nor_45_out, and_38_out);
  and and_39 (and_39_out, not_22_out, and_1_out);
  nor nor_45 (nor_45_out, and_39_out, nor_43_out);
  nor nor_46 (nor_45_out, and_39_out, nor_43_out);
  not not_23 (not_23_out, and_12_out);
  and and_40 (and_40_out, and_1_out, and_12_out);
  nor nor_47 (nor_47_out, nor_49_out, and_40_out);
  nor nor_48 (nor_47_out, nor_49_out, and_40_out);
  and and_41 (and_41_out, not_23_out, and_1_out);
  nor nor_49 (nor_49_out, and_41_out, nor_47_out);
  nor nor_50 (nor_49_out, and_41_out, nor_47_out);
  and and_42 (and_42_out, and_1_out, and_13_out);
  nor nor_51 (nor_51_out, nor_53_out, and_42_out);
  nor nor_52 (nor_51_out, nor_53_out, and_42_out);
  not not_24 (not_24_out, and_13_out);
  and and_43 (and_43_out, not_24_out, and_1_out);
  nor nor_53 (nor_53_out, and_43_out, nor_51_out);
  nor nor_54 (nor_53_out, and_43_out, nor_51_out);
  not not_25 (not_25_out, and_14_out);
  and and_44 (and_44_out, and_1_out, and_14_out);
  nor nor_55 (nor_55_out, nor_57_out, and_44_out);
  nor nor_56 (nor_55_out, nor_57_out, and_44_out);
  and and_45 (and_45_out, not_25_out, and_1_out);
  nor nor_57 (nor_57_out, and_45_out, nor_55_out);
  nor nor_58 (nor_57_out, and_45_out, nor_55_out);
  not not_26 (not_26_out, and_15_out);
  and and_46 (and_46_out, and_1_out, and_15_out);
  nor nor_59 (nor_59_out, nor_61_out, and_46_out);
  nor nor_60 (nor_59_out, nor_61_out, and_46_out);
  and and_47 (and_47_out, not_26_out, and_1_out);
  nor nor_61 (nor_61_out, and_47_out, nor_59_out);
  nor nor_62 (nor_61_out, and_47_out, nor_59_out);
  and and_48 (and_15_out, nor_61_out, undriven_35);
  and and_49 (and_14_out, nor_57_out, undriven_35);
  and and_50 (and_13_out, nor_53_out, undriven_35);
  and and_51 (and_12_out, nor_49_out, undriven_35);
  and and_52 (and_11_out, nor_45_out, undriven_35);
  and and_53 (and_10_out, nor_41_out, undriven_35);
  and and_54 (and_9_out, nor_39_out, undriven_35);
  and and_55 (and_8_out, nor_33_out, undriven_35);
  and and_56 (and_7_out, nor_29_out, undriven_35);
  and and_57 (and_6_out, nor_27_out, undriven_35);
  and and_58 (and_5_out, nor_21_out, undriven_35);
  and and_59 (and_4_out, nor_17_out, undriven_35);
  and and_60 (and_60_out, nor_13_out, undriven_35);
  and and_61 (and_61_out, nor_11_out, undriven_35);
  and and_62 (and_62_out, nor_5_out, undriven_35);
  and and_63 (and_63_out, nor_2_out, undriven_35);
  and and_64 (and_64_out, undriven_2, undriven_3);
  and and_65 (and_65_out, undriven_2, undriven_19);
  and and_66 (and_66_out, undriven_3, undriven_19);
  and and_67 (and_67_out, or_1_out, undriven_4);
  and and_68 (and_68_out, or_1_out, undriven_20);
  and and_69 (and_69_out, undriven_4, undriven_20);
  and and_70 (and_70_out, or_2_out, undriven_5);
  and and_71 (and_71_out, or_2_out, undriven_21);
  and and_72 (and_72_out, undriven_5, undriven_21);
  and and_73 (and_73_out, or_3_out, undriven_6);
  and and_74 (and_74_out, or_3_out, undriven_22);
  and and_75 (and_75_out, undriven_6, undriven_22);
  and and_76 (and_76_out, or_4_out, undriven_7);
  and and_77 (and_77_out, or_4_out, undriven_23);
  and and_78 (and_78_out, undriven_7, undriven_23);
  and and_79 (and_79_out, or_5_out, undriven_8);
  and and_80 (and_80_out, or_5_out, undriven_24);
  and and_81 (and_81_out, undriven_8, undriven_24);
  and and_82 (and_82_out, or_6_out, undriven_9);
  and and_83 (and_83_out, or_6_out, undriven_25);
  and and_84 (and_84_out, undriven_9, undriven_25);
  and and_85 (and_85_out, or_7_out, undriven_10);
  and and_86 (and_86_out, or_7_out, undriven_26);
  and and_87 (and_87_out, undriven_10, undriven_26);
  and and_88 (and_88_out, or_8_out, undriven_11);
  and and_89 (and_89_out, or_8_out, undriven_27);
  and and_90 (and_90_out, undriven_11, undriven_27);
  and and_91 (and_91_out, or_9_out, undriven_12);
  and and_92 (and_92_out, or_9_out, undriven_28);
  and and_93 (and_93_out, undriven_12, undriven_28);
  and and_94 (and_94_out, or_10_out, undriven_13);
  and and_95 (and_95_out, or_10_out, undriven_29);
  and and_96 (and_96_out, undriven_13, undriven_29);
  and and_97 (and_97_out, or_11_out, undriven_14);
  and and_98 (and_98_out, or_11_out, undriven_30);
  and and_99 (and_99_out, undriven_14, undriven_30);
  and and_100 (and_100_out, or_12_out, undriven_15);
  and and_101 (and_101_out, or_12_out, undriven_31);
  and and_102 (and_102_out, undriven_15, undriven_31);
  and and_103 (and_103_out, or_13_out, undriven_16);
  and and_104 (and_104_out, or_13_out, undriven_32);
  and and_105 (and_105_out, undriven_16, undriven_32);
  and and_106 (and_106_out, or_14_out, undriven_17);
  and and_107 (and_107_out, or_14_out, undriven_33);
  and and_108 (and_108_out, undriven_17, undriven_33);
  and and_109 (and_109_out, or_15_out, undriven_18);
  and and_110 (and_110_out, or_15_out, undriven_34);
  and and_111 (and_111_out, undriven_18, undriven_34);
  or or_1 (or_1_out, and_64_out, and_65_out, and_66_out);
  or or_2 (or_2_out, and_67_out, and_68_out, and_69_out);
  or or_3 (or_3_out, and_70_out, and_71_out, and_72_out);
  or or_4 (or_4_out, and_73_out, and_74_out, and_75_out);
  or or_5 (or_5_out, and_76_out, and_77_out, and_78_out);
  or or_6 (or_6_out, and_79_out, and_80_out, and_81_out);
  or or_7 (or_7_out, and_82_out, and_83_out, and_84_out);
  or or_8 (or_8_out, and_85_out, and_86_out, and_87_out);
  or or_9 (or_9_out, and_88_out, and_89_out, and_90_out);
  or or_10 (or_10_out, and_91_out, and_92_out, and_93_out);
  or or_11 (or_11_out, and_94_out, and_95_out, and_96_out);
  or or_12 (or_12_out, and_97_out, and_98_out, and_99_out);
  or or_13 (or_13_out, and_100_out, and_101_out, and_102_out);
  or or_14 (or_14_out, and_103_out, and_104_out, and_105_out);
  or or_15 (or_15_out, and_106_out, and_107_out, and_108_out);
  or or_16 (or_16_out, and_109_out, and_110_out, and_111_out);
  xor xor_1 (xor_1_out, undriven_3, undriven_19);
  xor xor_2 (xor_2_out, undriven_4, undriven_20);
  xor xor_3 (xor_3_out, undriven_5, undriven_21);
  xor xor_4 (xor_4_out, undriven_6, undriven_22);
  xor xor_5 (xor_5_out, undriven_7, undriven_23);
  xor xor_6 (xor_6_out, undriven_8, undriven_24);
  xor xor_7 (xor_7_out, undriven_9, undriven_25);
  xor xor_8 (xor_8_out, undriven_10, undriven_26);
  xor xor_9 (xor_9_out, undriven_11, undriven_27);
  xor xor_10 (xor_10_out, undriven_12, undriven_28);
  xor xor_11 (xor_11_out, undriven_13, undriven_29);
  xor xor_12 (xor_12_out, undriven_14, undriven_30);
  xor xor_13 (xor_13_out, undriven_15, undriven_31);
  xor xor_14 (xor_14_out, undriven_16, undriven_32);
  xor xor_15 (xor_15_out, undriven_17, undriven_33);
  xor xor_16 (xor_16_out, undriven_18, undriven_34);
  xor xor_17 (xor_17_out, xor_1_out, undriven_2);
  xor xor_18 (xor_18_out, xor_2_out, or_1_out);
  xor xor_19 (xor_19_out, xor_3_out, or_2_out);
  xor xor_20 (xor_20_out, xor_4_out, or_3_out);
  xor xor_21 (xor_21_out, xor_5_out, or_4_out);
  xor xor_22 (xor_22_out, xor_6_out, or_5_out);
  xor xor_23 (xor_23_out, xor_7_out, or_6_out);
  xor xor_24 (xor_24_out, xor_8_out, or_7_out);
  xor xor_25 (xor_25_out, xor_9_out, or_8_out);
  xor xor_26 (xor_26_out, xor_10_out, or_9_out);
  xor xor_27 (xor_27_out, xor_11_out, or_10_out);
  xor xor_28 (xor_28_out, xor_12_out, or_11_out);
  xor xor_29 (xor_29_out, xor_13_out, or_12_out);
  xor xor_30 (xor_30_out, xor_14_out, or_13_out);
  xor xor_31 (xor_31_out, xor_15_out, or_14_out);
  xor xor_32 (xor_32_out, xor_16_out, or_15_out);
  and and_112 (and_112_out, undriven, xor_32_out);
  and and_113 (and_113_out, undriven, xor_31_out);
  and and_114 (and_114_out, undriven, xor_30_out);
  and and_115 (and_115_out, undriven, xor_29_out);
  and and_116 (and_116_out, undriven, xor_28_out);
  and and_117 (and_117_out, undriven, xor_27_out);
  and and_118 (and_118_out, undriven, xor_26_out);
  and and_119 (and_119_out, undriven, xor_25_out);
  and and_120 (and_120_out, undriven, xor_24_out);
  and and_121 (and_121_out, undriven, xor_23_out);
  and and_122 (and_122_out, undriven, xor_22_out);
  and and_123 (and_123_out, undriven, xor_21_out);
  and and_124 (and_124_out, undriven, xor_20_out);
  and and_125 (and_125_out, undriven, xor_19_out);
  and and_126 (and_126_out, undriven, xor_18_out);
  and and_127 (and_127_out, undriven, xor_17_out);
endmodule
